// Logisim project Combined.circ as structural Verilog: 1 circuit, main circuit main
module main (
  input  Reset,
  output [1:0] out_2
);

  wire clock_1_out, main_2_jalr, main_2_out_3, main_2_out_4, main_2_out_5, main_2_out_6, main_2_out_7,
       main_4_out_4;
  wire [1:0] main_2_out_8, main_2_out_9;
  wire [2:0] main_2_out_12, rom_1_data_2;
  wire [3:0] alu_controller_1_direction_3;
  wire [31:0] adder_1_out, main_1_out_4, main_1_out_5, main_1_out_6, main_3_out_8, main_3_out_9,
       main_5_out_4, multiplexer_1_out, multiplexer_2_out, multiplexer_3_out, multiplexer_4_out,
       multiplexer_5_out, PC_q, ram_1_data, rom_1_data;

  Multiplexer #(.select(2), .width(32), .enable("false")) multiplexer_1 (
    .in0(adder_1_out), .in1(main_1_out_5), .in2(main_1_out_6), .in3(main_5_out_4), .out(multiplexer_1_out),
    .sel(out_2));
  Register #(.width(32)) PC (.D(multiplexer_1_out), .Q(PC_q), .clk(clock_1_out), .clr(Reset));  // open: en
  Clock clock_1 (.out(clock_1_out));
  Adder #(.width(32)) adder_1 (.a(PC_q), .b(32'h4), .out(adder_1_out));  // open: cin, cout
  ROM #(.addrWidth(10), .dataWidth(32)) rom_1 (
    .addr(PC_q[11:2]), .data({rom_1_data[31:15], rom_1_data_2, rom_1_data[11:0]}));  // open: sel
  immediate_block_main main_1 (
    .out_4(main_1_out_4), .out_5(main_1_out_5), .out_6(main_1_out_6), .in_3(main_2_out_9),
    .in_2({rom_1_data[31:15], rom_1_data_2, rom_1_data[11:0]}), .in_1(PC_q));
  Completed_Controller_main main_2 (
    .in_1(rom_1_data[6:0]), .out_12(main_2_out_12), .out_3(main_2_out_3), .in_2(main_4_out_4),
    .out_4(main_2_out_4), .out_5(main_2_out_5), .out_6(main_2_out_6), .out_7(main_2_out_7),
    .out_8(main_2_out_8), .out_9(main_2_out_9), .out_10(out_2), .jalr(main_2_jalr));
  Register_Files_Block_main main_3 (
    .in_4(main_2_out_7), .in_1(multiplexer_5_out), .in_5(rom_1_data[19:15]), .in_7(rom_1_data[24:20]),
    .out_8(main_3_out_8), .out_9(main_3_out_9), .in_6(rom_1_data[11:7]), .in_2(Reset), .in_3(clock_1_out));
  Multiplexer #(.select(2), .width(32), .enable("false")) multiplexer_2 (
    .in0(main_3_out_8), .in1(adder_1_out), .in2(PC_q), .out(multiplexer_2_out), .sel(main_2_out_8));  // open: in3
  Multiplexer #(.width(32), .enable("false")) multiplexer_3 (
    .in0(main_3_out_9), .in1(main_1_out_4), .out(multiplexer_3_out), .sel(main_2_out_3));
  ALU_Branch_Controller_main main_4 (
    .in_1(main_3_out_8), .in_2(main_3_out_9), .out_4(main_4_out_4), .in_3(rom_1_data_2));
  ALU_COntroller alu_controller_1 (
    .Direction_3(alu_controller_1_direction_3), .Direction(main_2_out_12), .Direction_2(rom_1_data_2),
    .in_3(rom_1_data[30]));
  ALU_Circuit_main main_5 (
    .in_1(multiplexer_2_out), .in_2(multiplexer_3_out), .out_4(main_5_out_4),
    .in_3(alu_controller_1_direction_3));
  RAM #(.addrWidth(10), .dataWidth(32), .bus("separate")) ram_1 (
    .addr(main_5_out_4[11:2]), .din(main_3_out_9), .data(ram_1_data), .str(main_2_out_4), .clk(clock_1_out),
    .ld(main_2_out_5), .clr(Reset));  // open: sel
  Multiplexer #(.width(32), .enable("false")) multiplexer_4 (
    .in0(main_5_out_4), .in1(ram_1_data), .out(multiplexer_4_out), .sel(main_2_out_6));
  Multiplexer #(.width(32), .enable("false")) multiplexer_5 (
    .in0(multiplexer_4_out), .in1(adder_1_out), .out(multiplexer_5_out), .sel(main_2_jalr));

  // Notes on the sheet:
  //   Clock
  //   Instructions Memory
  //   contents of rom_1 (hex, n*v repeats v):
  //   500113 500193 14000ef 120293 502023 2303 628663 310233 8067
  //   Register    Files
  //   Branch ALU
  //   Data Memory
  //   rd
endmodule
