// Logisim project ALU Circuit.circ as structural Verilog: 1 circuit, main circuit main
module main (
  input  [31:0] in_1,
  input  [31:0] in_2,
  input  [3:0] in_3,
  output [31:0] out_4
);

  wire [31:0] adder_1_out, and_1_out, comparator_1_gt, or_1_out, shifter_1_out, shifter_2_out, shifter_3_out,
       subtractor_1_out, xor_1_out;

  Adder #(.width(32)) adder_1 (.a(in_2), .b(in_1), .out(adder_1_out));  // open: cin, cout
  Subtractor #(.width(32)) subtractor_1 (.a(in_2), .b(in_1), .out(subtractor_1_out));  // open: bin, bout
  assign and_1_out = in_2 & in_1;  // AND_Gate and_1, 32 bits wide
  assign or_1_out = in_2 | in_1;  // OR_Gate or_1, 32 bits wide
  assign xor_1_out = in_2 ^ in_1;  // XOR_Gate xor_1, 32 bits wide
  Shifter #(.width(32)) shifter_1 (.in(in_2), .\dist (in_1[4:0]), .out(shifter_1_out));
  Shifter #(.width(32), .shift("lr")) shifter_2 (.in(in_2), .\dist (in_1[4:0]), .out(shifter_2_out));
  Shifter #(.width(32), .shift("ar")) shifter_3 (.in(in_2), .\dist (in_1[4:0]), .out(shifter_3_out));
  Comparator #(.width(32)) comparator_1 (.a(in_2), .b(in_1), .gt(comparator_1_gt[0]));  // open: eq, lt
  Multiplexer #(.select(4), .width(32), .enable("false")) multiplexer_1 (
    .in0(adder_1_out), .in1(subtractor_1_out), .in2(and_1_out), .in3(or_1_out), .in4(xor_1_out),
    .in5(shifter_1_out), .in6(shifter_2_out), .in7(shifter_3_out), .in8(comparator_1_gt), .out(out_4),
    .sel(in_3));  // open: in9, in10, in11, in12, in13, in14, in15
endmodule
