// Logisim project Alu Op-function.circ as structural Verilog: 2 circuits, main circuit main
module main (
);

  ALU_COntroller alu_controller_1 ();  // open: Direction_3, Direction, Direction_2, in_3
endmodule

module ALU_COntroller (
  input  [2:0] Direction,
  input  [2:0] Direction_2,
  input  in_3,
  output [3:0] Direction_3
);

  wire and_1_out, and_2_out, and_3_out, and_4_out, and_5_out, and_6_out, and_7_out, and_8_out, and_9_out,
       and_10_out, and_11_out, and_12_out, and_13_out, and_14_out, and_15_out, and_16_out, and_17_out,
       and_18_out, and_19_out, and_20_out, and_21_out, and_22_out, and_23_out, and_24_out, and_25_out,
       and_26_out, and_27_out, and_28_out, and_29_out, and_30_out, and_31_out, not_1_out, not_2_out,
       not_3_out, not_4_out, not_5_out, not_6_out, not_7_out, not_8_out, not_9_out, not_10_out, not_11_out,
       not_12_out, not_13_out, not_14_out, not_15_out, not_16_out, not_17_out, not_18_out, not_19_out,
       not_20_out, not_21_out, not_22_out, not_23_out, or_2_out, or_3_out, or_4_out, or_7_out, or_8_out,
       or_9_out;

  not not_1 (not_1_out, Direction[0]);
  not not_2 (not_2_out, Direction[2]);
  not not_3 (not_3_out, Direction_2[0]);
  not not_4 (not_4_out, Direction[0]);
  not not_5 (not_5_out, Direction_2[1]);
  not not_6 (not_6_out, Direction[2]);
  not not_7 (not_7_out, Direction[0]);
  not not_8 (not_8_out, Direction_2[0]);
  not not_9 (not_9_out, Direction_2[1]);
  not not_10 (not_10_out, Direction[0]);
  not not_11 (not_11_out, Direction[2]);
  not not_12 (not_12_out, Direction[0]);
  not not_13 (not_13_out, Direction[2]);
  and and_1 (and_1_out, not_1_out, not_2_out);
  and and_2 (and_2_out, not_3_out, Direction_2[1]);
  and and_3 (and_3_out, not_4_out, not_5_out);
  and and_4 (and_4_out, not_6_out, Direction_2[0]);
  not not_14 (not_14_out, Direction_2[1]);
  and and_5 (and_5_out, not_7_out, not_8_out);
  and and_6 (and_6_out, not_9_out, Direction_2[2]);
  and and_7 (and_7_out, not_10_out, Direction_2[2]);
  and and_8 (and_8_out, not_11_out, Direction_2[0]);
  and and_9 (and_9_out, not_12_out, not_13_out);
  not not_15 (not_15_out, Direction_2[0]);
  not not_16 (not_16_out, Direction_2[1]);
  not not_17 (not_17_out, Direction[0]);
  not not_18 (not_18_out, Direction_2[0]);
  and and_10 (and_10_out, and_1_out, and_2_out);
  and and_11 (and_11_out, Direction[0], Direction[1]);
  and and_12 (and_12_out, and_3_out, Direction_2[2]);
  and and_13 (and_13_out, and_4_out, not_14_out);
  and and_14 (and_14_out, and_5_out, and_6_out);
  and and_15 (and_15_out, and_7_out, in_3);
  and and_16 (and_16_out, and_8_out, Direction_2[1]);
  and and_17 (and_17_out, Direction[0], Direction[1]);
  and and_18 (and_18_out, and_9_out, not_15_out);
  and and_19 (and_19_out, not_16_out, in_3);
  and and_20 (and_20_out, not_17_out, not_18_out);
  not not_19 (not_19_out, Direction[0]);
  not not_20 (not_20_out, Direction_2[1]);
  not not_21 (not_21_out, in_3);
  not not_22 (not_22_out, Direction[0]);
  not not_23 (not_23_out, Direction_2[2]);
  or or_1 (Direction_3[0], and_10_out, and_11_out);
  or or_2 (or_2_out, and_12_out, and_13_out);
  and and_21 (and_21_out, Direction[0], Direction[1]);
  or or_3 (or_3_out, and_14_out, and_15_out);
  or or_4 (or_4_out, and_16_out, and_17_out);
  and and_22 (and_22_out, and_18_out, and_19_out);
  and and_23 (and_23_out, and_20_out, Direction_2[2]);
  and and_24 (and_24_out, not_19_out, not_20_out);
  and and_25 (and_25_out, Direction_2[2], not_21_out);
  and and_26 (and_26_out, not_22_out, Direction_2[0]);
  and and_27 (and_27_out, Direction_2[1], not_23_out);
  and and_28 (and_28_out, Direction[0], Direction[1]);
  or or_5 (Direction_3[1], or_2_out, and_21_out);
  or or_6 (Direction_3[2], or_3_out, or_4_out);
  or or_7 (or_7_out, and_22_out, and_23_out);
  or or_8 (or_8_out, or_7_out, and_29_out);
  and and_29 (and_29_out, and_24_out, and_25_out);
  and and_30 (and_30_out, and_26_out, and_27_out);
  or or_9 (or_9_out, and_30_out, and_31_out);
  and and_31 (and_31_out, and_28_out, Direction[2]);
  or or_10 (Direction_3[3], or_8_out, or_9_out);

  // Notes on the sheet:
  //   Func 2
  //   Funct 7
  //   Alu Op 2
  //   Alu Op 1
  //   Alu Op 0
  //   Func 1
  //   Funct 0
  //   Pin 1 / Out 3
  //   Pin 1 / Out 3
  //   Pin 3 / Out 1
  //   Pin 4 / Out 0
endmodule
