// Logisim project CPU Fetch Stage.circ as structural Verilog: 1 circuit, main circuit main
module main (
  input  Reset,
  input  [1:0] in_2
);

  wire clock_1_out;
  wire [1:0] undriven_4;
  wire [31:0] adder_1_out, multiplexer_1_out, Program_Counter_q, rom_1_data, undriven, undriven_2,
       undriven_3, undriven_5;

  Multiplexer #(.select(2), .width(32)) multiplexer_1 (
    .in0(adder_1_out), .in1(undriven), .in2(undriven_2), .in3(undriven_3), .out(multiplexer_1_out),
    .sel(undriven_4));  // open: en
  Adder #(.width(32)) adder_1 (.a(undriven_5), .out(adder_1_out));  // open: b, cin, cout
  Register #(.width(32)) Program_Counter (
    .D(multiplexer_1_out), .Q(Program_Counter_q), .clk(clock_1_out), .clr(Reset));  // open: en
  Clock clock_1 (.out(clock_1_out));
  ROM #(.addrWidth(10), .dataWidth(32)) rom_1 (.addr(Program_Counter_q[9:0]), .data(rom_1_data));  // open: sel
  // Register_Files_Block_main main_1: pin names not known
endmodule
