// Logisim project Completed Controller.circ as structural Verilog: 1 circuit, main circuit main
module main (
  input  [6:0] in_1,
  input  in_2,
  output out_3,
  output out_4,
  output out_5,
  output out_6,
  output out_7,
  output [1:0] out_8,
  output [1:0] out_9,
  output [1:0] out_10,
  output jalr,
  output [2:0] out_12
);

  wire main_1_out_2, main_1_out_3, main_1_out_4, main_1_out_5, main_1_out_6, main_1_out_7, main_1_out_8,
       main_1_out_10;

  Decoder_main main_1 (
    .in_1(in_1), .out_2(main_1_out_2), .out_3(main_1_out_3), .out_4(main_1_out_4), .out_5(main_1_out_5),
    .out_6(main_1_out_6), .out_7(main_1_out_7), .out_8(main_1_out_8), .out_9(jalr), .out_10(main_1_out_10));
  Type_Decoder_main main_2 (
    .OPB_Select(out_3), .Mem_Write(out_4), .mem_read(out_5), .write_back(out_6), .reg_file_enable(out_7),
    .opA_sel(out_8), .imm_se(out_9), .pc_sel(out_10), .R(main_1_out_2), .I(main_1_out_4), .S(main_1_out_3),
    .B(main_1_out_6), .lui(main_1_out_8), .AUIPC(main_1_out_5), .JAL(jalr), .JALR(main_1_out_7),
    .LW(main_1_out_10), .B_Out(in_2));
  ALU_Instructions alu_instructions_1 (
    .R(main_1_out_2), .I(main_1_out_4), .S(main_1_out_3), .AUIPC(main_1_out_5), .LUI(main_1_out_8),
    .LW(main_1_out_10), .JALR(main_1_out_7), .JAL(jalr), .out_9(out_12));
endmodule
