// Logisim project Decoder.circ as structural Verilog: 1 circuit, main circuit main
module main (
  input  [6:0] in_1,
  output out_2,
  output out_3,
  output out_4,
  output out_5,
  output out_6,
  output out_7,
  output out_8,
  output out_9,
  output out_10
);

  Comparator #(.width(7)) comparator_1 (.a(in_1), .b(7'b0110011), .eq(out_2));  // open: gt, lt
  Comparator #(.width(7)) comparator_2 (.a(in_1), .b(7'b0100011), .eq(out_3));  // open: gt, lt
  Comparator #(.width(7)) comparator_3 (.a(in_1), .b(7'b0010011), .eq(out_4));  // open: gt, lt
  Comparator #(.width(7)) comparator_4 (.a(in_1), .b(7'b0010111), .eq(out_5));  // open: gt, lt
  Comparator #(.width(7)) comparator_5 (.a(in_1), .b(7'b1100011), .eq(out_6));  // open: gt, lt
  Comparator #(.width(7)) comparator_6 (.a(in_1), .b(7'b1100111), .eq(out_7));  // open: gt, lt
  Comparator #(.width(7)) comparator_7 (.a(in_1), .b(7'b0110111), .eq(out_8));  // open: gt, lt
  Comparator #(.width(7)) comparator_8 (.a(in_1), .b(7'b1101111), .eq(out_9));  // open: gt, lt
  Comparator #(.width(7)) comparator_9 (.a(in_1), .b(7'b0000011), .eq(out_10));  // open: gt, lt

  // Notes on the sheet:
  //   R-TYPE
  //   S-TYPE
  //   I-TYPE
  //   AUIpc-TYPE
  //   JALR-TYPE
  //   LUI-TYPE
  //   UJ-TYPE
  //   LW-TYPE
  //   SB-TYPE
endmodule
