// Logisim project Type Decoder.circ as structural Verilog: 1 circuit, main circuit main
module main (
  input  R,
  input  I,
  input  S,
  input  B,
  input  lui,
  input  AUIPC,
  input  JAL,
  input  JALR,
  input  LW,
  input  B_Out,
  output OPB_Select,
  output Mem_Write,
  output mem_read,
  output write_back,
  output reg_file_enable,
  output [1:0] opA_sel,
  output [1:0] imm_se,
  output [1:0] pc_sel
);

  wire and_1_out;

  and and_1 (and_1_out, B, B_Out);
  or or_1 (OPB_Select, I, S, lui, AUIPC, JALR, LW);
  or or_2 (write_back, JAL, LW);
  or or_3 (reg_file_enable, R, I, lui, AUIPC, JAL, JALR, LW);
  or or_4 (opA_sel[0], AUIPC, lui);
  or or_5 (opA_sel[1], lui, JAL);
  or or_6 (imm_se[0], JAL, B, S, R);
  or or_7 (imm_se[1], R, B, lui, AUIPC, JAL);
  or or_8 (pc_sel[0], and_1_out, JALR);
  or or_9 (pc_sel[1], JALR, JALR);

  assign mem_read = LW;
  assign Mem_Write = S;

  // Notes on the sheet:
  //   lsb
  //   msb
  //   lsb
  //   msb
  //   lsb
  //   msb
endmodule
