// Logisim project immediate block.circ as structural Verilog: 1 circuit, main circuit main
module main (
  input  [31:0] in_1,
  input  [31:0] in_2,
  input  [1:0] in_3,
  output [31:0] out_4,
  output [31:0] out_5,
  output [31:0] out_6
);

  wire [10:0] bit_extender_1_out_2;
  wire [19:11] bit_extender_1_out;
  wire [31:0] shifter_1_out;

  assign {bit_extender_1_out, bit_extender_1_out_2} = {{19{1'b0}}, in_2[31]};  // Bit_Extender bit_extender_1
  Shifter #(.width(32)) shifter_1 (
    .in({bit_extender_1_out[11], bit_extender_1_out_2, in_2[31:12]}), .\dist (5'b01100), .out(shifter_1_out));
  Adder #(.width(32)) adder_1 (
    .a({in_2[31], in_2[19:12], in_2[20], in_2[30:21], 1'b0, bit_extender_1_out_2}), .b(in_1), .out(out_5));  // open: cin, cout
  Multiplexer #(.select(2), .width(32), .enable("false")) multiplexer_1 (
    .in0({bit_extender_1_out, bit_extender_1_out_2, in_2[31:20]}),
    .in1({bit_extender_1_out, bit_extender_1_out_2, in_2[31:25], in_2[11:7]}), .in2(shifter_1_out),
    .out(out_4), .sel(in_3));  // open: in3
  Adder #(.width(32)) adder_2 (
    .a({bit_extender_1_out[18:11], bit_extender_1_out_2, in_2[31], in_2[7], in_2[30:25], in_2[11:8], 1'b0}),
    .b(in_1), .out(out_6));  // open: cin, cout

  // Notes on the sheet:
  //   I
  //   S
  //   s
  //   U
  //   J
  //   B
  //   J
  //   B
  //   I
  //   S
  //   U
  //   J
  //   B
endmodule
